# Fritzing sketch FuncGen_24a-Fritzing (saved by Fritzing 1.0.3b)
breadboards: 1
perfboards: 1

parts:
  J1 = female pin header, 4 pins [form="♀ (female)"]
  J2 = female pin header, 4 pins [form="♀ (female)"]  # not connected
  J3 = female pin header, 4 pins [form="♀ (female)"]  # not connected
  J4 = female pin header, 10 pins [form="♀ (female)"]  # not connected
  J5 = female pin header, 20 pins [form="♀ (female)"]
  J6 = female pin header, 20 pins [form="♀ (female)"]
  J7 = female pin header, 20 pins [form="♀ (female)"]
  A1 = Raspberry Pi Pico W
  C1 = Ceramic Capacitor [capacitance=100nF voltage=35V package="100 mil [THT, multilayer]"]
  R1 = Resistor [tolerance=±5% resistance=220 package="2010 [SMD]"]

nets:
  N1: J1.pin1, J5.pin7, R1.Pin_0
  N2: J1.pin2, J5.pin10, C1.1
  N3: J5.pin9, C1.0, R1.Pin_1
  N4: J6.pin1, A1.pin_40
  N5: J6.pin2, A1.pin_39
  N6: J6.pin3, J6.pin8, J6.pin13, J6.pin18, J7.pin3, J7.pin8, J7.pin13, J7.pin18, A1.pin_3, A1.pin_8, A1.pin_13, A1.pin_18, A1.pin_23, A1.pin_28, A1.pin_33, A1.pin_38
  N7: J6.pin4, A1.pin_37
  N8: J6.pin5, A1.pin_36
  N9: J6.pin6, A1.pin_35
  N10: J6.pin7, A1.pin_34
  N11: J6.pin9, A1.pin_32
  N12: J6.pin10, A1.pin_31
  N13: J6.pin11, A1.pin_30
  N14: J6.pin12, A1.pin_29
  N15: J6.pin14, A1.pin_27
  N16: J6.pin15, A1.pin_26
  N17: J6.pin16, A1.pin_25
  N18: J6.pin17, A1.pin_24
  N19: J6.pin19, A1.pin_22
  N20: J6.pin20, A1.pin_21
  N21: J7.pin1, A1.pin_1
  N22: J7.pin2, A1.pin_2
  N23: J7.pin4, A1.pin_4
  N24: J7.pin5, A1.pin_5
  N25: J7.pin6, A1.pin_6
  N26: J7.pin7, A1.pin_7
  N27: J7.pin9, A1.pin_9
  N28: J7.pin10, A1.pin_10
  N29: J7.pin11, A1.pin_11
  N30: J7.pin12, A1.pin_12
  N31: J7.pin14, A1.pin_14
  N32: J7.pin15, A1.pin_15
  N33: J7.pin16, A1.pin_16
  N34: J7.pin17, A1.pin_17
  N35: J7.pin19, A1.pin_19
  N36: J7.pin20, A1.pin_20

notes:
  VSIG
  GNDV
  VDAC
  GND
  +3.3V
  GP27 ADC1
  GP26 ADC0
  R1
  C1

custom parts:
  Raspberry Pi Pico W: Raspberry Pi Pico W. Based around the RP2040 microcontroller the Pico W is a low cost microcontroller device bringing Raspberry Pi quality, cost, and easy of use to the microcontroller space. The areas marked KEEPOUT in pcb silkscreen should not have traces running through them to avoid shorts on a soldered in module!
