# Fritzing sketch Preamplifier (saved by Fritzing 1.0.3b)
breadboards: 1

parts:
  IC1 = Dual Op-Amp [package=dip08]  # not connected
  R3 = Resistor [tolerance=±5% resistance=1.5k package="2010 [SMD]"]
  R4 = Resistor [tolerance=±5% resistance=10M package="2010 [SMD]"]
  C4 = Ceramic Capacitor [capacitance=100nF voltage=35V package="200 mil [THT, multilayer]"]
  C5 = Tantalum Capacitor [capacitance="1 μF" voltage=35V package="D 7343 [SMD, tantalum]"]
  R5 = Vertical Resistor [tolerance=±5% resistance=100k package=THT]
  R6 = Resistor [tolerance=±5% resistance=10k package="2010 [SMD]"]
  C3 = Ceramic Capacitor [capacitance=100nF voltage=35V package="200 mil [THT, multilayer]"]
  R2 = Vertical Resistor [tolerance=±5% resistance=10M package=THT]
  P1 = S1133 Si Photodiode [package="8mm Ceramic [THT]"]

nets:
  N1: R3.Pin_0, C3.1
  N2: R3.Pin_1, R4.Pin_1, C4.1, C5.-, R6.Pin_1
  N3: R4.Pin_0, R2.Pin_0, P1.cathode
  N4: C4.0, C5.+
  N5: R5.Pin_0, R6.Pin_0
  N6: C3.0, R2.Pin_1

notes:
  GND
  3.3V
  Pulse Out

custom parts:
  Vertical Resistor: A generic resistor (0.25W)
