# Fritzing sketch Preamplifier_V2 (saved by Fritzing 1.0.3b)
breadboards: 1

parts:
  IC1 = Dual Op-Amp [package=dip08]
  R1 = Vertical Resistor [tolerance=±5% resistance=10M package=THT]
  R3 = Resistor [tolerance=±5% resistance=10M package="0402 [SMD]"]
  C2 = Tantalum Capacitor [capacitance="1 μF" voltage=35V package="B 3528 [SMD, tantalum]"]
  P1 = S1133 Si Photodiode [package="8mm Ceramic [THT]"]
  C3 = Ceramic Capacitor [capacitance="100 nF" voltage=35V package="1206 [SMD, multilayer]"]
  C4 = Ceramic Capacitor [capacitance="100 nF" voltage=35V package="1206 [SMD, multilayer]"]
  R4 = Resistor [tolerance=±5% resistance=1.5k package="0402 [SMD]"]
  R5 = Vertical Resistor [tolerance=±5% resistance=100k package=THT]
  R6 = Resistor [tolerance=±5% resistance=10k package="0402 [SMD]"]

nets:
  N1: IC1.A_OUT, R1.Pin_1, C4.0
  N2: IC1.A_-IN, R1.Pin_0, P1.cathode
  N3: IC1.A_+IN, R3.Pin_1, P1.anode
  N4: IC1.A_V-, R3.Pin_0, C2.-, C3.0, R4.Pin_0, R6.Pin_1
  N5: IC1.B_+IN, C4.1, R4.Pin_1
  N6: IC1.B_-IN, R5.Pin_1, R6.Pin_0
  N7: IC1.B_OUT, R5.Pin_0
  N8: IC1.A_V+, C2.+, C3.1

custom parts:
  Vertical Resistor: A generic resistor (0.25W)
